# Fritzing sketch sketch (saved by Fritzing 0.9.3b)

parts:
  Parça1 = HX711 Weighing Sensor Module
  Parça2 = Adafruit ADS1115 16Bit I2C ADC [part_number="Adafruit #1085"]
  Parça3 = Arduino Nano (Rev3.0)
  J1 = female pin header, 3 pins [form="♀ (female)"]
  J2 = female pin header, 4 pins [form="♀ (female)"]

nets:
  VCC: Parça1.VCC, Parça3.5V, J1.pin3
  GND: Parça1.GND, Parça2.GND, Parça3.GND, J1.pin1
  N1: Parça1.DO/RX, Parça3.D3
  N2: Parça1.CK/TX, Parça3.D2
  N3: Parça1.E+, J2.pin4
  N4: Parça1.E-, J2.pin3
  N5: Parça1.A+, J2.pin2
  N6: Parça1.A-, J2.pin1
  N7: Parça2.AIN0, J1.pin2
  N8: Parça2.SDA, Parça3.A4
  N9: Parça2.SCL, Parça3.A5

notes:
  LOAD-CELL
  Red E+
  Black E-
  White A-
  Green A+
  LVDT
  Brown 5V
  Red A0
  Orange GND

custom parts:
  HX711 Weighing Sensor Module: HX711 is a precision 24-bit analog-to-digital converter (ADC) designed for weigh scales and industrial control applications to interface directly with a bridge sensor.
  Adafruit ADS1115 16Bit I2C ADC: For microcontrollers without an analog-to-digital converter or when you want a higher-precision ADC, the ADS1115 provides 16-bit precision at 860 samples/second over I2C. The chip can be configured as 4 single-ended input channels, or two differential channels. As a nice bonus, it even includes a programmable gain amplifier, up to x16, to help boost up smaller single/differential signals to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
